// Logisim project alu.circ as structural Verilog: 1 circuit, main circuit main
module main (
  input  [31:0] X,
  input  [31:0] Y,
  input  [3:0] Switch,
  output Equal,
  output [31:0] Result
);

  wire comparator_1_lt;
  wire [31:0] add, \and , div, mulh, mult, \or , rem, sll, slt, srl, \xor ;

  Shifter #(.width(32)) shifter_1 (.in(X), .\dist (Y[4:0]), .out(sll));
  Shifter #(.width(32), .shift("lr")) shifter_2 (.in(X), .\dist (Y[4:0]), .out(srl));
  Adder #(.width(32)) adder_1 (.a(X), .b(Y), .out(add));  // open: cin, cout
  assign \and  = X & Y;  // AND_Gate and_1, 32 bits wide
  assign \or  = X | Y;  // OR_Gate or_1, 32 bits wide
  assign \xor  = X ^ Y;  // XOR_Gate xor_1, 32 bits wide
  Comparator #(.width(32)) comparator_1 (.a(X), .b(Y), .eq(Equal), .lt(comparator_1_lt));  // open: gt
  Multiplier #(.width(32)) multiplier_1 (.a(X), .b(Y), .out(mult), .cout(mulh));  // open: cin
  Divider #(.width(32)) divider_1 (.a(X), .b(Y), .out(div), .rem(rem));  // open: upper
  Multiplexer #(.width(32)) multiplexer_1 (.in0(X), .in1(Y), .out(slt), .sel(comparator_1_lt));  // open: en
  Multiplexer #(.select(4), .width(32)) multiplexer_2 (
    .in0(sll), .in1(srl), .in2(add), .in3(\and ), .in4(\or ), .in5(\xor ), .in6(slt), .in7(mult), .in8(mulh),
    .in9(div), .in10(rem), .out(Result), .sel(Switch));  // open: in11, in12, in13, in14, in15, en

  // Other names for the same wires on the sheet: S[3:0] = Switch

  // Notes on the sheet:
  //   INPUTS to your circuit
  //   DON'T CHANGE THE LOCATIONS OF THE INPUTS AND OUTPUTS!
  //   OUTPUTS from your circuit
endmodule
