// Logisim project cpu.circ as structural Verilog: 3 circuits, main circuit main
module main (
  input  [31:0] INSTRUCTION,
  input  CLOCK,
  output [31:0] FETCH_ADDRESS,
  output [31:0] s0_Value,
  output [31:0] s1_Value,
  output [31:0] t0_Value,
  output [31:0] t1_Value,
  output [31:0] a0_Value,
  output [31:0] ra_Value,
  output [31:0] sp_Value
);

  wire ASel, BrEq, BrLT, BrUn, BSel, MEM_p1, MEM_p3, MEM_p9, MEM_p12, MemRW, PCSel, RegWEn;
  wire [1:0] WBSel;
  wire [2:0] ImmSel;
  wire [3:0] ALUSel;
  wire [31:0] alu, DataA, DataB, Imm, mem, multiplexer_1_out, multiplexer_2_out, multiplexer_3_out, pc,
       pc___4, wb;

  Multiplexer #(.width(32)) multiplexer_1 (.in0(pc___4), .in1(alu), .out(multiplexer_1_out), .sel(PCSel));  // open: en
  // Imm__Gen imm_gen_1: pin names not known; wires that end beside it: ImmSel, INSTRUCTION, Imm
  Register #(.width(32)) u_PC (.D(multiplexer_1_out), .Q(pc), .clk(CLOCK));  // open: en, clr
  Adder #(.width(32)) adder_1 (.a(pc), .b(32'h4), .out(pc___4));  // open: cin, cout
  regfile_main main_1 (
    .Read_Register_1__rs1(INSTRUCTION[11:7]), .Read_Register_2__rs2(INSTRUCTION[19:15]),
    .Write_Register__rd(INSTRUCTION[24:20]), .Write_Data(wb), .Write_Enable(RegWEn), .Clock(CLOCK),
    .Read_Data_1(DataA), .Read_Data_2(DataB), .s1_Value(s1_Value), .t0_Value(t0_Value), .t1_Value(t1_Value),
    .a0_Value(a0_Value), .s0_Value(s0_Value), .ra_Value(ra_Value), .sp_Value(sp_Value));
  Multiplexer #(.width(32), .enable("false")) multiplexer_2 (
    .in0(pc), .in1(DataA), .out(multiplexer_2_out), .sel(ASel));
  Multiplexer #(.width(32), .enable("false")) multiplexer_3 (
    .in0(DataB), .in1(Imm), .out(multiplexer_3_out), .sel(BSel));
  alu_main main_2 (.Switch(ALUSel), .X(multiplexer_2_out), .Result(alu), .Y(multiplexer_3_out));  // open: Equal
  Branch_Comp Branch_Comp (.in_1(DataA), .in_2(DataB), .BrUn(BrUn), .BrEq(BrEq), .BrLT(BrLT));
  Multiplexer #(.select(2), .width(32), .enable("false")) multiplexer_4 (
    .in0(pc___4), .in2(alu), .in3(mem), .out(wb), .sel(WBSel));  // open: in1
  // mem_main MEM: pin names not known; wires that end beside it: MEM_p1, MEM_p1, MEM_p3, alu, DataB, MemRW, MEM_p3, CLOCK, MEM_p9, mem, MEM_p9, MEM_p12

  // Other names for the same wires on the sheet: a0[31:0] = a0_Value; clk = CLOCK; fetch_addr[31:0] = FETCH_ADDRESS;
  //   AddrD[4:0] = INSTRUCTION[11:7]; AddrA[4:0] = INSTRUCTION[19:15]; AddrB[4:0] = INSTRUCTION[24:20];
  //   ra[31:0] = ra_Value; s0[31:0] = s0_Value; s1[31:0] = s1_Value; sp[31:0] = sp_Value; t0[31:0] = t0_Value;
  //   t1[31:0] = t1_Value

  // Notes on the sheet:
  //   Output
  //   These are outputs/inputs from run.circ
  //   Inputs
  //   These are DEBUG/TEST outputs from your circuit.
endmodule

module Branch_Comp (
  input  [31:0] in_1,
  input  [31:0] in_2,
  input  BrUn,
  output BrEq,
  output BrLT
);

  wire comparator_1_lt, comparator_2_lt;

  Comparator #(.width(32)) comparator_1 (.a(in_1), .b(in_2), .eq(BrEq), .lt(comparator_1_lt));  // open: gt
  Comparator #(.width(32)) comparator_2 (.a(in_1), .b(in_2), .lt(comparator_2_lt));  // open: gt, eq
  Multiplexer multiplexer_1 (.in0(comparator_1_lt), .in1(comparator_2_lt), .out(BrLT), .sel(BrUn));  // open: en

  // Other names for the same wires on the sheet: A[31:0] = in_1; B[31:0] = in_2
endmodule

module Imm__Gen (
  input  [31:0] in_1,
  input  [2:0] in_2,
  output [31:0] To_Instr_Mem
);

  wire [31:0] B_Type, I_Type, J_Type, S_Type, U_Type;

  assign I_Type = {{20{in_1[31]}}, in_1[31:20]};  // Bit_Extender bit_extender_1
  assign S_Type = {{20{in_1[31]}}, {in_1[31:25], in_1[11:7]}};  // Bit_Extender bit_extender_2
  assign U_Type = {{12{in_1[31]}}, in_1[31:12]};  // Bit_Extender bit_extender_3
  assign B_Type = {{19{in_1[31]}}, {in_1[31], in_1[7], in_1[30:25], in_1[11:8], 1'b0}};  // Bit_Extender bit_extender_4
  assign J_Type = {{11{in_1[31]}}, {in_1[31], in_1[19:12], in_1[20], in_1[30:21], 1'b0}};  // Bit_Extender bit_extender_5
  Multiplexer #(.select(3), .width(32), .enable("false")) multiplexer_1 (
    .in0(I_Type), .in1(S_Type), .in2(B_Type), .in3(U_Type), .in4(J_Type), .out(To_Instr_Mem), .sel(in_2));  // open: in5, in6, in7

  // Other names for the same wires on the sheet: Input[31:0] = in_1; Imm[31:0] = To_Instr_Mem
endmodule
