// Logisim project regfile.circ as structural Verilog: 1 circuit, main circuit main
module main (
  input  [4:0] Read_Register_1__rs1,
  input  [4:0] Read_Register_2__rs2,
  input  [4:0] Write_Register__rd,
  input  [31:0] Write_Data,
  input  Write_Enable,
  input  Clock,
  output [31:0] s0_Value,
  output [31:0] s1_Value,
  output [31:0] t0_Value,
  output [31:0] t1_Value,
  output [31:0] a0_Value,
  output [31:0] ra_Value,
  output [31:0] sp_Value,
  output [31:0] Read_Data_1,
  output [31:0] Read_Data_2
);

  wire write_x1, write_x2, write_x5, write_x6, write_x8, write_x9, write_x10, write_x11;
  wire [31:0] a1_out, x0_out;

  Demultiplexer #(.select(5)) demultiplexer_1 (
    .out1(write_x1), .out2(write_x2), .out5(write_x5), .out6(write_x6), .out8(write_x8), .out9(write_x9),
    .out10(write_x10), .out11(write_x11), .in(Write_Enable), .sel(Write_Register__rd));  // open: out0, out3, out4, out7, out12, out13, out14, out15, out16, out17, out18, out19, out20, out21, out22, out23, out24, out25, out26, out27, out28, out29, out30, out31, en
  Register #(.width(32)) x0 (.en(1'b0), .Q(x0_out), .clk(Clock));  // open: D, clr
  Register #(.width(32)) x5_t0 (.D(Write_Data), .en(write_x5), .Q(t0_Value), .clk(Clock));  // open: clr
  Register #(.width(32)) x9_s1 (.D(Write_Data), .en(write_x9), .Q(s1_Value), .clk(Clock));  // open: clr
  Register #(.width(32)) x1_ra (.D(Write_Data), .en(write_x1), .Q(ra_Value), .clk(Clock));  // open: clr
  Register #(.width(32)) x6_t1 (.D(Write_Data), .en(write_x6), .Q(t1_Value), .clk(Clock));  // open: clr
  Register #(.width(32)) x10_a0 (.D(Write_Data), .en(write_x10), .Q(a0_Value), .clk(Clock));  // open: clr
  Multiplexer #(.select(5), .width(32)) multiplexer_1 (
    .in0(x0_out), .in1(ra_Value), .in2(sp_Value), .in5(t0_Value), .in6(t1_Value), .in8(s0_Value),
    .in9(s1_Value), .in10(a0_Value), .in11(a1_out), .out(Read_Data_1), .sel(Read_Register_1__rs1));  // open: in3, in4, in7, in12, in13, in14, in15, in16, in17, in18, in19, in20, in21, in22, in23, in24, in25, in26, in27, in28, in29, in30, in31, en
  Register #(.width(32)) x2_sp (.D(Write_Data), .en(write_x2), .Q(sp_Value), .clk(Clock));  // open: clr
  Register #(.width(32)) x8_s0 (.D(Write_Data), .en(write_x8), .Q(s0_Value), .clk(Clock));  // open: clr
  Register #(.width(32)) x11_a1 (.D(Write_Data), .en(write_x11), .Q(a1_out), .clk(Clock));  // open: clr
  Multiplexer #(.select(5), .width(32)) multiplexer_2 (
    .in0(x0_out), .in1(ra_Value), .in2(sp_Value), .in5(t0_Value), .in6(t1_Value), .in8(s0_Value),
    .in9(s1_Value), .in10(a0_Value), .in11(a1_out), .out(Read_Data_2), .sel(Read_Register_2__rs2));  // open: in3, in4, in7, in12, in13, in14, in15, in16, in17, in18, in19, in20, in21, in22, in23, in24, in25, in26, in27, in28, in29, in30, in31, en

  // Other names for the same wires on the sheet: a0_out[31:0] = a0_Value; clk = Clock; ra_out[31:0] = ra_Value;
  //   read_data1[31:0] = Read_Data_1; read_data2[31:0] = Read_Data_2; read_reg1[4:0] = Read_Register_1__rs1;
  //   read_reg2[4:0] = Read_Register_2__rs2; s0_out[31:0] = s0_Value; s1_out[31:0] = s1_Value;
  //   sp_out[31:0] = sp_Value; t0_out[31:0] = t0_Value; t1_out[31:0] = t1_Value; write_en = Write_Enable;
  //   write_reg[4:0] = Write_Register__rd

  // Notes on the sheet:
  //   INPUTS to your circuit
  //   These are DEBUG/TEST outputs from your circuit.
  //   DON'T CHANGE THE LOCATIONS OF THE INPUTS AND OUTPUTS!
  //   OUTPUTS from your circuit
endmodule
